# Fritzing sketch LCR_meter (saved by Fritzing 0.9.3b)
breadboards: 1

parts:
  R1 = Resistor [tolerance=±5% resistance=220 package=THT]
  R2 = Resistor [tolerance=±5% resistance=10k package=THT]
  Grove1 = Grove OLED 128x96
  S1 = Pushbutton [package="[THT]"]
  S2 = Pushbutton [package="[THT]"]
  J3 = Screw terminal - 2 pins [package=THT]
  J1 = screw terminal, 2 pins
  J1_2 = Screw terminal - 2 pins [package=THT]
  Part2 = Arduino Nano (Rev3.0) (ICSP)

nets:
  N1: R1.Pin_0, R2.Pin_1, J1.pin2, J1_2.pin2, Part2.A7
  N2: R1.Pin_1, Part2.D11/MOSI
  N3: R2.Pin_0, Part2.D12/MISO
  GND: Grove1.GND, S1.Pin_3, S1.Pin_4, S2.Pin_3, S2.Pin_4, J1.pin1, J1_2.pin1, Part2.D3, Part2.D8, Part2.GND
  VCC: Grove1.VCC, Part2.5V
  N4: Grove1.SDA, Part2.A4
  N5: Grove1.SCL, Part2.A5
  N6: S1.Pin_1, S1.Pin_2
  N7: S2.Pin_1, S2.Pin_2
  N8: J3.pin1, Part2.A2
  N9: J3.pin2, Part2.A3

notes:
  test1
  terminal
  test2
  terminal
